// Logisim project comp01.circ as structural Verilog: 19 circuits, main circuit main
module main (
  input  in_1,
  input  in_2,
  input  in_3,
  input  in_4,
  input  in_5,
  input  in_6,
  input  in_7,
  output out_8,
  output out_9,
  output out_10,
  output out_11,
  output out_12,
  output out_13
);

  wire and_1_out, cornerr_1_out_2, cornerr_2_out_2, cornerr_3_out_2, cross_1_out_3, cross_1_out_4,
       cross_2_out_3, cross_2_out_4, cross_3_out_3, cross_3_out_4, cross_4_out_3, cross_5_out_3,
       cross_6_out_3, delay_1_out_2, delay_2_out_2, not_1_out, or_1_out, or_2_out;

  fulladder fulladder_1 ();  // open: in_2, in_1, out_3
  not not_1 (not_1_out, in_7);
  or or_1 (or_1_out, in_6, not_1_out);
  and and_1 (and_1_out, or_1_out, in_7);
  // NAND_Gate nand_1 is placed but not wired
  \and  and_2 ();  // open: in_1, in_2, out_3
  delay delay_1 (.in_1(in_5), .out_2(delay_1_out_2));
  and and_3 (out_13, or_1_out, or_2_out);
  or or_2 (or_2_out, and_1_out, out_13);
  delay delay_2 (.in_1(delay_1_out_2), .out_2(delay_2_out_2));
  delay delay_3 (.in_1(delay_2_out_2), .out_2(out_12));
  // NAND_Gate nand_2 is placed but not wired
  cornerR cornerr_1 (.in_1(in_1), .out_2(cornerr_1_out_2));
  \cross  cross_1 (.in_2(in_2), .in_1(cornerr_1_out_2), .out_4(cross_1_out_4), .out_3(cross_1_out_3));
  cornerR cornerr_2 (.in_1(cross_1_out_3), .out_2(cornerr_2_out_2));
  \cross  cross_2 (.in_2(cross_3_out_3), .in_1(cornerr_2_out_2), .out_4(cross_2_out_4), .out_3(cross_2_out_3));
  \cross  cross_3 (.in_2(in_3), .in_1(cross_1_out_4), .out_4(cross_3_out_4), .out_3(cross_3_out_3));
  \cross  cross_4 (.in_2(in_4), .in_1(cross_3_out_4), .out_4(out_8), .out_3(cross_4_out_3));
  \cross  cross_5 (.in_2(cross_4_out_3), .in_1(cross_2_out_4), .out_4(out_9), .out_3(cross_5_out_3));
  cornerR cornerr_3 (.in_1(cross_2_out_3), .out_2(cornerr_3_out_2));
  \cross  cross_6 (.in_2(cross_5_out_3), .in_1(cornerr_3_out_2), .out_4(out_10), .out_3(cross_6_out_3));
  cornerR cornerr_4 (.in_1(cross_6_out_3), .out_2(out_11));
endmodule

module delay (
  input  in_1,
  output out_2
);

  wire clock_1_out;

  Shift_Register #(.length(1)) shift_register_1 (
    .shift(1'b1), .in(in_1), .clk(clock_1_out), .out(out_2));  // open: load, clr, d0, q0
  Clock clock_1 (.out(clock_1_out));
endmodule

module cornerR (
  input  in_1,
  output out_2
);

  delay delay_1 (.in_1(in_1), .out_2(out_2));
endmodule

module cornerL (
  input  in_1,
  output out_2
);

  delay delay_1 (.in_1(in_1), .out_2(out_2));
endmodule

module \cross  (
  input  in_1,
  input  in_2,
  output out_3,
  output out_4
);

  delay delay_1 (.in_1(in_1), .out_2(out_4));
  delay delay_2 (.in_1(in_2), .out_2(out_3));
endmodule

module \and  (
  input  in_1,
  input  in_2,
  output out_3
);

  wire delay_1_out_2, delay_2_out_2;

  delay delay_1 (.in_1(in_1), .out_2(delay_1_out_2));
  delay delay_2 (.in_1(in_2), .out_2(delay_2_out_2));
  and and_1 (out_3, delay_1_out_2, delay_2_out_2);
endmodule

module addR (
  input  in_1,
  input  in_2,
  output out_3
);

  wire delay_1_out_2, delay_2_out_2;

  delay delay_1 (.in_1(in_1), .out_2(delay_1_out_2));
  delay delay_2 (.in_1(in_2), .out_2(delay_2_out_2));
  and and_1 (out_3, delay_1_out_2, delay_2_out_2);
endmodule

module addL (
  input  in_1,
  input  in_2,
  output out_3
);

  wire delay_1_out_2, delay_2_out_2;

  delay delay_1 (.in_1(in_2), .out_2(delay_1_out_2));
  delay delay_2 (.in_1(in_1), .out_2(delay_2_out_2));
  and and_1 (out_3, delay_2_out_2, delay_1_out_2);
endmodule

module \or  (
  input  in_1,
  input  in_2,
  output out_3
);

  wire delay_1_out_2, delay_2_out_2;

  delay delay_1 (.in_1(in_1), .out_2(delay_1_out_2));
  delay delay_2 (.in_1(in_2), .out_2(delay_2_out_2));
  or or_1 (out_3, delay_1_out_2, delay_2_out_2);
endmodule

module orR (
  input  in_1,
  input  in_2,
  output out_3
);

  wire delay_1_out_2, delay_2_out_2;

  delay delay_1 (.in_1(in_2), .out_2(delay_1_out_2));
  delay delay_2 (.in_1(in_1), .out_2(delay_2_out_2));
  or or_1 (out_3, delay_2_out_2, delay_1_out_2);
endmodule

module orL (
  input  in_1,
  input  in_2,
  output out_3
);

  wire delay_1_out_2, delay_2_out_2;

  delay delay_1 (.in_1(in_1), .out_2(delay_1_out_2));
  delay delay_2 (.in_1(in_2), .out_2(delay_2_out_2));
  or or_1 (out_3, delay_1_out_2, delay_2_out_2);
endmodule

module \xor  (
  input  in_1,
  input  in_2,
  output out_3
);

  wire delay_1_out_2, delay_2_out_2;

  delay delay_1 (.in_1(in_1), .out_2(delay_1_out_2));
  delay delay_2 (.in_1(in_2), .out_2(delay_2_out_2));
  xor xor_1 (out_3, delay_1_out_2, delay_2_out_2);
endmodule

module xorR (
  input  in_1,
  input  in_2,
  output out_3
);

  wire delay_1_out_2, delay_2_out_2;

  delay delay_1 (.in_1(in_2), .out_2(delay_1_out_2));
  delay delay_2 (.in_1(in_1), .out_2(delay_2_out_2));
  xor xor_1 (out_3, delay_2_out_2, delay_1_out_2);
endmodule

module xorL (
  input  in_1,
  input  in_2,
  output out_3
);

  wire delay_1_out_2, delay_2_out_2;

  delay delay_1 (.in_1(in_2), .out_2(delay_1_out_2));
  delay delay_2 (.in_1(in_1), .out_2(delay_2_out_2));
  xor xor_1 (out_3, delay_2_out_2, delay_1_out_2);
endmodule

module fulladder (
  input  in_1,
  input  in_2,
  output out_3
);

  wire addl_1_out_3, and_1_out_3, cornerl_1_out_2, cornerl_2_out_2, cornerl_3_out_2, cornerr_1_out_2,
       cornerr_2_out_2, cross_1_out_3, cross_1_out_4, cross_2_out_3, cross_2_out_4, delay_1_out_2,
       ds2_1_out_2, ds2_2_out_2, orl_1_out_3, split_1_out_2, split_1_out_3, splitl_1_out_2, splitl_1_out_3,
       splitr_1_out_2, splitr_1_out_3, splitr_2_out_2, splitr_2_out_3, xorl_1_out_3;

  ds2 ds2_1 (.in_1(in_2), .out_2(ds2_1_out_2));
  cornerL cornerl_1 (.in_1(splitr_1_out_3), .out_2(cornerl_1_out_2));
  ds2 ds2_2 (.in_1(in_1), .out_2(ds2_2_out_2));
  cornerR cornerr_1 (.in_1(splitl_1_out_2), .out_2(cornerr_1_out_2));
  splitL splitl_1 (.in_1(ds2_2_out_2), .out_2(splitl_1_out_2), .out_3(splitl_1_out_3));
  xorL xorl_1 (.in_2(splitl_1_out_3), .in_1(splitr_1_out_2), .out_3(xorl_1_out_3));
  splitR splitr_1 (.in_1(ds2_1_out_2), .out_3(splitr_1_out_3), .out_2(splitr_1_out_2));
  delay delay_1 (.in_1(cornerl_1_out_2), .out_2(delay_1_out_2));
  \cross  cross_1 (.in_2(xorl_1_out_3), .in_1(cornerr_1_out_2), .out_4(cross_1_out_4), .out_3(cross_1_out_3));
  splitR splitr_2 (.in_1(cross_1_out_3), .out_3(splitr_2_out_3), .out_2(splitr_2_out_2));
  addL addl_1 (.in_2(cross_1_out_4), .in_1(delay_1_out_2), .out_3(addl_1_out_3));
  \cross  cross_2 (.in_2(addl_1_out_3), .in_1(splitr_2_out_3), .out_4(cross_2_out_4), .out_3(cross_2_out_3));
  cornerL cornerl_2 (.in_1(cross_2_out_4), .out_2(cornerl_2_out_2));
  \and  and_1 (.in_1(splitr_2_out_2), .in_2(cornerl_3_out_2), .out_3(and_1_out_3));
  cornerL cornerl_3 (.in_1(split_1_out_2), .out_2(cornerl_3_out_2));
  orL orl_1 (.in_2(and_1_out_3), .in_1(cross_2_out_3), .out_3(orl_1_out_3));
  split split_1 (.in_1(orl_1_out_3), .out_2(split_1_out_2), .out_3(split_1_out_3));
  cornerR cornerr_2 (.in_1(split_1_out_3), .out_2(cornerr_2_out_2));
  \xor  xor_1 (.in_1(cornerl_2_out_2), .in_2(cornerr_2_out_2), .out_3(out_3));
endmodule

module splitR (
  input  in_1,
  output out_2,
  output out_3
);

  delay delay_1 (.in_1(in_1), .out_2(out_2));

  assign out_3 = out_2;
endmodule

module splitL (
  input  in_1,
  output out_2,
  output out_3
);

  delay delay_1 (.in_1(in_1), .out_2(out_2));

  assign out_3 = out_2;
endmodule

module split (
  input  in_1,
  output out_2,
  output out_3
);

  delay delay_1 (.in_1(in_1), .out_2(out_2));

  assign out_3 = out_2;
endmodule

module ds2 (
  input  in_1,
  output out_2
);

  wire clock_1_out, t_ff_1_q;

  Shift_Register #(.length(1)) shift_register_1 (
    .shift(1'b1), .in(in_1), .clk(t_ff_1_q), .out(out_2));  // open: load, clr, d0, q0
  Clock clock_1 (.out(clock_1_out));
  T_Flip_Flop t_ff_1 (.clk(clock_1_out), .T(clock_1_out), .Q(t_ff_1_q), .en(1'b1));  // open: Qn, preset, reset
endmodule
